// Logisim project P0_CRC.circ as structural Verilog: 2 circuits, main circuit CRC
module CRC (
  input  [7:0] A,
  input  [3:0] B,
  output [10:0] out_3
);

  wire C0, C1, C2, C3, C4, C5, C6, C7;
  wire [3:1] out1, out2, out3, out4, out5, out6, out7;

  // Probe on out1
  divider divider (.C(B), .B(A[7:4]), .out_3(out1), .out_4(C0));
  // Probe on out2
  divider divider_2 (.C(B), .B({out1, A[3]}), .out_3(out2), .out_4(C1));
  // Probe on out3
  divider divider_3 (.C(B), .B({out2, A[2]}), .out_3(out3), .out_4(C2));
  // Probe on out4
  divider divider_4 (.C(B), .B({out3, A[1]}), .out_3(out4), .out_4(C3));
  // Probe on out5
  divider divider_5 (.C(B), .B({out4, A[0]}), .out_3(out5), .out_4(C4));
  // Probe on out6
  divider divider_6 (.C(B), .B({out5, 1'b0}), .out_3(out6), .out_4(C5));
  // Probe on out7
  divider divider_7 (.C(B), .B({out6, 1'b0}), .out_3(out7), .out_4(C6));
  divider divider_8 (.C(B), .B({out7, 1'b0}), .out_3(out_3[2:0]), .out_4(C7));

  assign out_3[10:3] = A;

  // Other names for the same wires on the sheet: out1[0] = A[3]; out2[0] = A[2]; out3[0] = A[1]; out4[0] = A[0];
  //   out8[2:0] = out_3[2:0]; in1[3:0] = A[7:4]
endmodule

module divider (
  input  [3:0] C,
  input  [3:0] B,
  output [2:0] out_3,
  output out_4
);

  wire not_1_out;
  wire [3:0] xor_1_out;
  wire [3:3] multiplexer_1_out;

  xor xor_1 (xor_1_out[0], C[0], B[0]);
  xor xor_2 (xor_1_out[1], C[1], B[1]);
  xor xor_3 (xor_1_out[2], C[2], B[2]);
  xor xor_4 (xor_1_out[3], C[3], B[3]);
  not not_1 (not_1_out, B[3]);
  // Probe on B
  Multiplexer #(.width(4)) multiplexer_1 (
    .in0(xor_1_out), .in1(B), .out({multiplexer_1_out[3], out_3}), .sel(not_1_out));  // open: en

  assign out_4 = B[3];
endmodule
