// Logisim project P0_FSM.circ as structural Verilog: 3 circuits, main circuit fsm
module fsm (
  input  in_1,
  input  [1:0] in_2,
  output out_3
);

  wire clk;
  wire [2:0] multiplexer_1_out, register_1_q, trans_1_s0_;

  Clock clock_1 (.out(clk));
  trans trans_1 (
    .s2(register_1_q[2]), .s1(register_1_q[1]), .s0(register_1_q[0]), .in1(in_2[1]), .in0(in_2[0]),
    .s2_(trans_1_s0_[2]), .s1_(trans_1_s0_[1]), .s0_(trans_1_s0_[0]));
  Multiplexer #(.width(3)) multiplexer_1 (
    .in0(trans_1_s0_), .in1(3'b000), .out(multiplexer_1_out), .sel(in_1));  // open: en
  Register #(.width(3)) register_1 (.D(multiplexer_1_out), .Q(register_1_q), .clk(clk));  // open: en, clr
  \output  output_1 (
    .s2(register_1_q[2]), .s1(register_1_q[1]), .s0(register_1_q[0]), .in1(in_2[1]), .in0(in_2[0]), .Z(out_3));

  // Other names for the same wires on the sheet: clr = in_1; in[1:0] = in_2
endmodule

module trans (
  input  s2,
  input  s1,
  input  s0,
  input  in1,
  input  in0,
  output s2_,
  output s1_,
  output s0_
);

  wire and_2_out, and_3_out, and_4_out, and_5_out, and_6_out, and_7_out, not_1_out, not_2_out, not_3_out,
       not_4_out, not_5_out, not_6_out, not_7_out, not_8_out, not_9_out;

  not not_1 (not_1_out, in0);
  not not_2 (not_2_out, s1);
  not not_3 (not_3_out, s0);
  not not_4 (not_4_out, s1);
  not not_5 (not_5_out, s0);
  not not_6 (not_6_out, s1);
  not not_7 (not_7_out, in0);
  not not_8 (not_8_out, s0);
  not not_9 (not_9_out, in0);
  and and_1 (s2_, s1, s0, not_1_out);
  and and_2 (and_2_out, not_2_out, s0);
  and and_3 (and_3_out, s1, not_3_out);
  and and_4 (and_4_out, not_4_out, not_5_out, in0);
  and and_5 (and_5_out, not_6_out, s0, not_7_out);
  and and_6 (and_6_out, s1, not_8_out, not_9_out);
  and and_7 (and_7_out, s1, s0, in0);
  or or_1 (s1_, and_2_out, and_3_out);
  or or_2 (s0_, and_4_out, and_5_out, and_6_out, and_7_out);
endmodule

module \output  (
  input  s2,
  input  s1,
  input  s0,
  input  in1,
  input  in0,
  output Z
);

  wire not_1_out, not_2_out;

  not not_1 (not_1_out, s2);
  not not_2 (not_2_out, in0);
  and and_1 (Z, not_1_out, s1, s0, not_2_out);
endmodule
