// Logisim project P0_GRF.circ as structural Verilog: 1 circuit, main circuit grf
module grf (
  input  [4:0] in_1,
  input  in_2,
  input  in_3,
  input  in_4,
  input  [4:0] in_5,
  input  [4:0] in_6,
  input  [31:0] in_7,
  input  [2:0] in_8,
  output [31:0] out_9,
  output [31:0] out_10
);

  wire [31:0] r0_out, r1, r1_out, r2, r2_out, r3, r3_out, r4, r4_out, r5, r5_out, r6, r6_out, r7, r7_out, r8,
       r8_out, r9, r9_out, r10, r10_out, r11, r11_out, r12, r12_out, r13, r13_out, r14, r14_out, r15,
       r15_out, r16, r16_out, r17, r17_out, r18, r18_out, r19, r19_out, r20, r20_out, r21, r21_out, r22,
       r22_out, r23, r23_out, r24, r24_out, r25, r25_out, r26, r26_out, r27, r27_out, r28, r28_out, r29,
       r29_out, r30, r30_out, r31, r31_out;

  Demultiplexer #(.select(5), .width(32), .tristate("true")) demultiplexer_1 (
    .out1(r1), .out2(r2), .out3(r3), .out4(r4), .out5(r5), .out6(r6), .out7(r7), .out8(r8), .out9(r9),
    .out10(r10), .out11(r11), .out12(r12), .out13(r13), .out14(r14), .out15(r15), .out16(r16), .out17(r17),
    .out18(r18), .out19(r19), .out20(r20), .out21(r21), .out22(r22), .out23(r23), .out24(r24), .out25(r25),
    .out26(r26), .out27(r27), .out28(r28), .out29(r29), .out30(r30), .out31(r31), .in(in_7), .sel(in_6),
    .en(in_4));  // open: out0
  Decoder #(.select(3)) decoder_1 (.sel(in_8));  // open: out0, out1, out2, out3, out4, out5, out6, out7, en
  Register #(.width(32)) register_1 (.D({32{1'b0}}), .Q(r0_out), .clk(in_2), .clr(in_3));  // open: en
  Register #(.width(32)) register_2 (.D(r1), .Q(r1_out), .clk(in_2), .clr(in_3));  // open: en
  Register #(.width(32)) register_3 (.D(r2), .Q(r2_out), .clk(in_2), .clr(in_3));  // open: en
  Register #(.width(32)) register_4 (.D(r3), .Q(r3_out), .clk(in_2), .clr(in_3));  // open: en
  Register #(.width(32)) register_5 (.D(r4), .Q(r4_out), .clk(in_2), .clr(in_3));  // open: en
  Register #(.width(32)) register_6 (.D(r5), .Q(r5_out), .clk(in_2), .clr(in_3));  // open: en
  Register #(.width(32)) register_7 (.D(r6), .Q(r6_out), .clk(in_2), .clr(in_3));  // open: en
  Register #(.width(32)) register_8 (.D(r7), .Q(r7_out), .clk(in_2), .clr(in_3));  // open: en
  Register #(.width(32)) register_9 (.D(r8), .Q(r8_out), .clk(in_2), .clr(in_3));  // open: en
  Register #(.width(32)) register_10 (.D(r9), .Q(r9_out), .clk(in_2), .clr(in_3));  // open: en
  Register #(.width(32)) register_11 (.D(r10), .Q(r10_out), .clk(in_2), .clr(in_3));  // open: en
  Register #(.width(32)) register_12 (.D(r11), .Q(r11_out), .clk(in_2), .clr(in_3));  // open: en
  Register #(.width(32)) register_13 (.D(r12), .Q(r12_out), .clk(in_2), .clr(in_3));  // open: en
  Register #(.width(32)) register_14 (.D(r13), .Q(r13_out), .clk(in_2), .clr(in_3));  // open: en
  Register #(.width(32)) register_15 (.D(r14), .Q(r14_out), .clk(in_2), .clr(in_3));  // open: en
  Register #(.width(32)) register_16 (.D(r15), .Q(r15_out), .clk(in_2), .clr(in_3));  // open: en
  Multiplexer #(.select(5), .width(32), .disabled(0)) multiplexer_1 (
    .in0(r0_out), .in1(r1_out), .in2(r2_out), .in3(r3_out), .in4(r4_out), .in5(r5_out), .in6(r6_out),
    .in7(r7_out), .in8(r8_out), .in9(r9_out), .in10(r10_out), .in11(r11_out), .in12(r12_out), .in13(r13_out),
    .in14(r14_out), .in15(r15_out), .in16(r16_out), .in17(r17_out), .in18(r18_out), .in19(r19_out),
    .in20(r20_out), .in21(r21_out), .in22(r22_out), .in23(r23_out), .in24(r24_out), .in25(r25_out),
    .in26(r26_out), .in27(r27_out), .in28(r28_out), .in29(r29_out), .in30(r30_out), .in31(r31_out),
    .out(out_10), .sel(in_1), .en(1'b1));
  Register #(.width(32)) register_17 (.D(r16), .Q(r16_out), .clk(in_2), .clr(in_3));  // open: en
  Register #(.width(32)) register_18 (.D(r17), .Q(r17_out), .clk(in_2), .clr(in_3));  // open: en
  Register #(.width(32)) register_19 (.D(r18), .Q(r18_out), .clk(in_2), .clr(in_3));  // open: en
  Register #(.width(32)) register_20 (.D(r19), .Q(r19_out), .clk(in_2), .clr(in_3));  // open: en
  Register #(.width(32)) register_21 (.D(r20), .Q(r20_out), .clk(in_2), .clr(in_3));  // open: en
  Register #(.width(32)) register_22 (.D(r21), .Q(r21_out), .clk(in_2), .clr(in_3));  // open: en
  Register #(.width(32)) register_23 (.D(r22), .Q(r22_out), .clk(in_2), .clr(in_3));  // open: en
  Register #(.width(32)) register_24 (.D(r23), .Q(r23_out), .clk(in_2), .clr(in_3));  // open: en
  Register #(.width(32)) register_25 (.D(r24), .Q(r24_out), .clk(in_2), .clr(in_3));  // open: en
  Register #(.width(32)) register_26 (.D(r25), .Q(r25_out), .clk(in_2), .clr(in_3));  // open: en
  Register #(.width(32)) register_27 (.D(r26), .Q(r26_out), .clk(in_2), .clr(in_3));  // open: en
  Register #(.width(32)) register_28 (.D(r27), .Q(r27_out), .clk(in_2), .clr(in_3));  // open: en
  Multiplexer #(.select(5), .width(32), .disabled(0)) multiplexer_2 (
    .in0(r0_out), .in1(r1_out), .in2(r2_out), .in3(r3_out), .in4(r4_out), .in5(r5_out), .in6(r6_out),
    .in7(r7_out), .in8(r8_out), .in9(r9_out), .in10(r10_out), .in11(r11_out), .in12(r12_out), .in13(r13_out),
    .in14(r14_out), .in15(r15_out), .in16(r16_out), .in17(r17_out), .in18(r18_out), .in19(r19_out),
    .in20(r20_out), .in21(r21_out), .in22(r22_out), .in23(r23_out), .in24(r24_out), .in25(r25_out),
    .in26(r26_out), .in27(r27_out), .in28(r28_out), .in29(r29_out), .in30(r30_out), .in31(r31_out),
    .out(out_9), .sel(in_5), .en(1'b1));
  Register #(.width(32)) register_29 (.D(r28), .Q(r28_out), .clk(in_2), .clr(in_3));  // open: en
  Register #(.width(32)) register_30 (.D(r29), .Q(r29_out), .clk(in_2), .clr(in_3));  // open: en
  Register #(.width(32)) register_31 (.D(r30), .Q(r30_out), .clk(in_2), .clr(in_3));  // open: en
  Register #(.width(32)) register_32 (.D(r31), .Q(r31_out), .clk(in_2), .clr(in_3));  // open: en
  // Probe on nothing

  // Other names for the same wires on the sheet: A1[4:0] = in_1; A2[4:0] = in_5; A3[4:0] = in_6; clk = in_2;
  //   clr = in_3; WD[31:0] = in_7; WE = in_4
endmodule
