// Logisim project P0_navigation.circ as structural Verilog: 4 circuits, main circuit navigation
module navigation (
  input  [1:0] dir,
  input  clk,
  input  reset,
  output out_4,
  output out_5
);

  wire comparator_1_eq;
  wire [2:0] register_1_q, trans_1_s0_;

  trans trans_1 (
    .s2(register_1_q[2]), .s1(register_1_q[1]), .s0(register_1_q[0]), .dir1(dir[1]), .dir0(dir[0]),
    .s2_(trans_1_s0_[2]), .s1_(trans_1_s0_[1]), .s0_(trans_1_s0_[0]));  // open: hit
  Register #(.width(3)) register_1 (.D(trans_1_s0_), .Q(register_1_q), .clk(clk), .clr(reset));  // open: en
  output2 output2_1 (.s2(register_1_q[2]), .s1(register_1_q[1]), .s0(register_1_q[0]), .arrive(out_4));
  Comparator #(.width(3)) comparator_1 (.a(register_1_q), .b(trans_1_s0_), .eq(comparator_1_eq));  // open: gt, lt
  Register #(.width(1)) register_2 (.D(comparator_1_eq), .Q(out_5), .clk(clk), .clr(reset));  // open: en
endmodule

module trans (
  input  s2,
  input  s1,
  input  s0,
  input  dir1,
  input  dir0,
  output s2_,
  output s1_,
  output s0_,
  output hit
);

  wire and_1_out, and_2_out, and_3_out, and_4_out, and_5_out, and_6_out, and_7_out, and_8_out, and_9_out,
       and_10_out, and_11_out, and_12_out, and_13_out, and_14_out, and_15_out, and_16_out, and_17_out,
       not_1_out, not_2_out, not_3_out, not_4_out, not_5_out, not_6_out, not_7_out, not_8_out, not_9_out,
       not_10_out, not_11_out, not_12_out, not_13_out, not_14_out, not_15_out, not_16_out, not_17_out,
       not_18_out, not_19_out, not_20_out, not_21_out, not_22_out, not_23_out, not_24_out, not_25_out,
       not_26_out, not_27_out, not_28_out, not_29_out, not_30_out, not_31_out;

  not not_1 (not_1_out, s0);
  not not_2 (not_2_out, dir1);
  not not_3 (not_3_out, dir0);
  not not_4 (not_4_out, s2);
  not not_5 (not_5_out, dir1);
  not not_6 (not_6_out, dir1);
  not not_7 (not_7_out, dir0);
  not not_8 (not_8_out, s1);
  not not_9 (not_9_out, dir1);
  not not_10 (not_10_out, dir1);
  not not_11 (not_11_out, dir0);
  not not_12 (not_12_out, s0);
  not not_13 (not_13_out, dir1);
  not not_14 (not_14_out, s0);
  not not_15 (not_15_out, dir0);
  not not_16 (not_16_out, s2);
  not not_17 (not_17_out, s1);
  not not_18 (not_18_out, dir1);
  not not_19 (not_19_out, dir0);
  not not_20 (not_20_out, dir0);
  not not_21 (not_21_out, s2);
  not not_22 (not_22_out, s0);
  not not_23 (not_23_out, dir1);
  not not_24 (not_24_out, s2);
  not not_25 (not_25_out, s1);
  not not_26 (not_26_out, s0);
  not not_27 (not_27_out, s2);
  not not_28 (not_28_out, s0);
  not not_29 (not_29_out, dir0);
  not not_30 (not_30_out, dir1);
  not not_31 (not_31_out, dir0);
  and and_1 (and_1_out, s1, not_1_out, not_2_out, not_3_out);
  and and_2 (and_2_out, not_4_out, s1, s0, not_5_out, dir0);
  and and_3 (and_3_out, s2, s1, not_6_out, not_7_out);
  and and_4 (and_4_out, not_8_out, s0, not_9_out);
  and and_5 (and_5_out, s0, not_10_out, not_11_out);
  and and_6 (and_6_out, s1, not_12_out, not_13_out, dir0);
  and and_7 (and_7_out, s1, not_14_out, dir1, not_15_out);
  and and_8 (and_8_out, s1, s0, dir1, dir0);
  and and_9 (and_9_out, not_16_out, not_17_out, not_18_out, not_19_out);
  and and_10 (and_10_out, s0, dir1, dir0);
  and and_11 (and_11_out, s1, dir1, dir0);
  and and_12 (and_12_out, s1, s0, not_20_out);
  and and_13 (and_13_out, not_21_out, not_22_out, not_23_out, dir0);
  and and_14 (and_14_out, not_24_out, not_25_out, not_26_out, dir1);
  and and_15 (and_15_out, not_27_out, not_28_out, dir1, not_29_out);
  and and_16 (and_16_out, s0, dir1, dir0);
  and and_17 (and_17_out, s1, s0, not_30_out, not_31_out);
  or or_1 (s2_, and_1_out, and_2_out, and_3_out);
  or or_2 (s1_, and_4_out, and_5_out, and_6_out, and_7_out, and_8_out);
  or or_3 (s0_, and_9_out, and_10_out, and_11_out, and_12_out);
  or or_4 (hit, and_13_out, and_14_out, and_15_out, and_16_out, and_17_out);
endmodule

module \output  (
  input  s2,
  input  s1,
  input  s0,
  input  dir1,
  input  dir0,
  output arrive,
  output hit
);

  wire and_1_out, and_2_out, and_3_out, and_4_out, and_5_out, and_6_out, and_7_out, not_1_out, not_2_out,
       not_3_out, not_4_out, not_5_out, not_6_out, not_7_out, not_8_out, not_9_out, not_10_out, not_11_out,
       not_12_out;

  not not_1 (not_1_out, s0);
  not not_2 (not_2_out, dir1);
  not not_3 (not_3_out, dir0);
  not not_4 (not_4_out, dir1);
  not not_5 (not_5_out, s0);
  not not_6 (not_6_out, dir1);
  not not_7 (not_7_out, s1);
  not not_8 (not_8_out, s0);
  not not_9 (not_9_out, s0);
  not not_10 (not_10_out, dir0);
  not not_11 (not_11_out, dir1);
  not not_12 (not_12_out, dir0);
  and and_1 (and_1_out, s1, not_1_out, not_2_out, not_3_out);
  and and_2 (and_2_out, s1, s0, not_4_out, dir0);
  and and_3 (and_3_out, not_5_out, not_6_out, dir0);
  and and_4 (and_4_out, not_7_out, not_8_out, dir1);
  and and_5 (and_5_out, not_9_out, dir1, not_10_out);
  and and_6 (and_6_out, s0, dir1, dir0);
  and and_7 (and_7_out, s1, s0, not_11_out, not_12_out);
  or or_1 (arrive, and_1_out, and_2_out);
  or or_2 (hit, and_3_out, and_4_out, and_5_out, and_6_out, and_7_out);
endmodule

// output
module output2 (
  input  s2,
  input  s1,
  input  s0,
  output arrive
);


  assign arrive = s2;
endmodule
