// Logisim project 寄存器（写使，初始化，复位）.circ as structural Verilog: 1 circuit, main circuit main
module main (
  input  [31:0] in,
  input  en,
  input  clk,
  input  reset_yi,
  input  reset_tong,
  input  [31:0] init,
  output [31:0] out
);

  wire counter_1_carry;
  wire [31:0] multiplexer_1_out, multiplexer_2_out, register_1_q;

  Multiplexer #(.width(32)) multiplexer_1 (.in0(out), .in1(in), .out(multiplexer_1_out), .sel(en));  // open: en
  Pull_Resistor #(.pull(1)) pull_resistor_1 (.node(en));
  Pull_Resistor pull_resistor_2 (.node(reset_yi));
  Pull_Resistor pull_resistor_3 (.node(reset_tong));
  Pull_Resistor pull_resistor_4 (.node(init));
  Multiplexer #(.width(32)) multiplexer_2 (
    .in0(multiplexer_1_out), .in1(init), .out(multiplexer_2_out), .sel(reset_tong));  // open: en
  Register #(.width(32)) register_1 (.D(multiplexer_2_out), .Q(register_1_q), .clk(clk), .clr(reset_yi));  // open: en
  Counter #(.width(1), .max('h1), .ongoal("stay")) counter_1 (
    .carry(counter_1_carry), .clk(clk), .clr(reset_yi));  // open: load, D, count, Q
  Multiplexer #(.width(32)) multiplexer_3 (
    .in0(init), .in1(register_1_q), .out(out), .sel(counter_1_carry));  // open: en
endmodule
