// Logisim project 序列识别2021.circ as structural Verilog: 5 circuits, main circuit main
module main (
  input  [1:0] in_1,
  output out_2,
  output out_3
);

  wire clock_1_out;
  wire [2:0] trans_1_next, \状态存储_1_out_3 ;

  trans trans_1 (.state(\状态存储_1_out_3 ), .In(in_1), .next(trans_1_next));
  Clock clock_1 (.out(clock_1_out));
  \状态存储  \u_状态存储_1  (.in_1(trans_1_next), .clk(clock_1_out), .out_3(\状态存储_1_out_3 ));
  \输出逻辑  \u_输出逻辑_1  (.in_1(\状态存储_1_out_3 ), .in_2(in_1), .Out1(out_2), .out2(out_3));
endmodule

module \状态转移  (
  input  S2,
  input  S1,
  input  S0,
  input  In1,
  input  In0,
  output O2,
  output O1,
  output O0
);

  wire and_1_out, and_2_out, and_3_out, and_4_out, and_5_out, and_6_out, and_7_out, and_8_out, and_9_out,
       and_10_out, and_11_out, and_12_out, and_13_out, and_14_out, and_15_out, not_1_out, not_2_out,
       not_3_out, not_4_out, not_5_out, not_6_out, not_7_out, not_8_out, or_2_out;

  not not_1 (not_1_out, S2);
  not not_2 (not_2_out, S2);
  not not_3 (not_3_out, In1);
  not not_4 (not_4_out, In0);
  not not_5 (not_5_out, S2);
  not not_6 (not_6_out, S0);
  not not_7 (not_7_out, S2);
  not not_8 (not_8_out, S0);
  and and_1 (and_1_out, not_1_out, S1);
  and and_2 (and_2_out, S2, S0);
  and and_3 (and_3_out, not_2_out, S0);
  and and_4 (and_4_out, not_3_out, not_4_out);
  and and_5 (and_5_out, not_5_out, S1);
  and and_6 (and_6_out, not_6_out, In1);
  and and_7 (and_7_out, not_7_out, S1);
  and and_8 (and_8_out, not_8_out, In0);
  and and_9 (and_9_out, and_1_out, In0);
  or or_1 (O2, and_9_out, and_10_out);
  and and_10 (and_10_out, and_2_out, In0);
  and and_11 (and_11_out, and_3_out, and_4_out);
  or or_2 (or_2_out, and_11_out, and_12_out);
  and and_12 (and_12_out, and_5_out, and_6_out);
  and and_13 (and_13_out, S2, S0);
  and and_14 (and_14_out, and_13_out, In0);
  or or_3 (O0, In1, and_15_out);
  and and_15 (and_15_out, and_7_out, and_8_out);
  or or_4 (O1, or_2_out, and_14_out);
endmodule

module \状态存储  (
  input  [2:0] in_1,
  input  clk,
  output [2:0] out_3
);

  Register #(.width(3)) register_1 (.D(in_1), .Q(out_3), .clk(clk));  // open: en, clr
endmodule

module \输出逻辑  (
  input  [2:0] in_1,
  input  [1:0] in_2,
  output Out1,
  output out2
);

  wire and_1_out, and_2_out;

  and and_1 (and_1_out, in_1[1], in_1[0]);
  and and_2 (and_2_out, in_1[2], in_1[0]);
  and and_3 (Out1, and_1_out, in_2[0]);
  and and_4 (out2, and_2_out, in_2[0]);
endmodule

module trans (
  input  [2:0] state,
  input  [1:0] In,
  output [2:0] next
);

  \状态转移  \u_状态转移_1  (
    .S2(state[2]), .S1(state[1]), .S0(state[0]), .In1(In[1]), .In0(In[0]), .O2(next[2]), .O1(next[1]),
    .O0(next[0]));
endmodule
