// Logisim project mod5.circ as structural Verilog: 5 circuits, main circuit mod5
module mod5 (
  input  in_1,
  output out_2,
  output out_3,
  output out_4,
  output out_5,
  output out_6
);

  wire clock_1_out;
  wire [1:0] register_1_q, trans_1_out_3;

  trans trans_1 (.in_1(register_1_q), .in(in_1), .out_3(trans_1_out_3));
  Clock clock_1 (.out(clock_1_out));
  Register #(.width(2)) register_1 (.D(trans_1_out_3), .Q(register_1_q), .clk(clock_1_out));  // open: en, clr
  \output  output_1 (.in_1(register_1_q), .in(in_1), .s0(out_2), .s1(out_3), .s2(out_4), .s3(out_5), .s4(out_6));
endmodule

module trans (
  input  [1:0] in_1,
  input  in,
  output [1:0] out_3
);


  assign out_3 = {in_1[0], in};
endmodule

module \output  (
  input  [1:0] in_1,
  input  in,
  output s0,
  output s1,
  output s2,
  output s3,
  output s4
);

  wire not_1_out, not_2_out, not_3_out, not_4_out;

  not not_1 (not_1_out, in_1[0]);
  not not_2 (not_2_out, in);
  not not_3 (not_3_out, in_1[0]);
  and and_1 (s3, in_1[0], in);
  not not_4 (not_4_out, in);
  and and_2 (s1, not_1_out, not_2_out);
  and and_3 (s2, not_3_out, in);
  and and_4 (s4, in_1[0], not_4_out);

  assign s0 = 1'b0;
endmodule

module trans2 (
  input  [1:0] in_1,
  input  in,
  output [1:0] out_3
);

  wire and_1_out, and_2_out, and_3_out, and_4_out, not_1_out, not_2_out, not_3_out, not_4_out;

  not not_1 (not_1_out, in_1[0]);
  not not_2 (not_2_out, in_1[1]);
  not not_3 (not_3_out, in_1[1]);
  not not_4 (not_4_out, in);
  and and_1 (and_1_out, not_1_out, in);
  and and_2 (and_2_out, in_1[0], not_2_out);
  and and_3 (and_3_out, in_1[0], not_3_out, not_4_out);
  and and_4 (and_4_out, in_1[0], in_1[1], in);
  or or_1 (out_3[0], and_1_out, and_2_out);
  or or_2 (out_3[1], and_3_out, and_4_out);
endmodule

module output2 (
  input  [1:0] in_1,
  input  in,
  output s0,
  output s1,
  output s2,
  output s3,
  output s4
);

  wire and_1_out, and_2_out, and_3_out, and_4_out, and_5_out, and_6_out, and_7_out, and_8_out, not_1_out,
       not_2_out, not_3_out, not_4_out, not_5_out, not_6_out, not_7_out, not_8_out, not_9_out, not_10_out,
       not_11_out, not_12_out;

  not not_1 (not_1_out, in_1[0]);
  not not_2 (not_2_out, in_1[1]);
  not not_3 (not_3_out, in);
  not not_4 (not_4_out, in);
  not not_5 (not_5_out, in_1[0]);
  not not_6 (not_6_out, in_1[1]);
  not not_7 (not_7_out, in_1[0]);
  not not_8 (not_8_out, in_1[1]);
  not not_9 (not_9_out, in_1[0]);
  not not_10 (not_10_out, in);
  not not_11 (not_11_out, in_1[1]);
  not not_12 (not_12_out, in);
  and and_1 (and_1_out, not_1_out, not_2_out, not_3_out);
  or or_1 (s1, and_1_out, and_2_out);
  and and_2 (and_2_out, in_1[0], in_1[1], not_4_out);
  and and_3 (and_3_out, not_5_out, not_6_out, in);
  or or_2 (s2, and_3_out, and_4_out);
  and and_4 (and_4_out, in_1[0], in_1[1], in);
  and and_5 (and_5_out, not_7_out, in_1[1], in);
  or or_3 (s3, and_5_out, and_6_out);
  and and_6 (and_6_out, in_1[0], not_8_out, in);
  and and_7 (and_7_out, not_9_out, in_1[1], not_10_out);
  or or_4 (s4, and_7_out, and_8_out);
  and and_8 (and_8_out, in_1[0], not_11_out, not_12_out);

  assign s0 = 1'b0;
endmodule
