// Logisim project swap.circ as structural Verilog: 4 circuits, main circuit 4bit_sort
module _1bit_swap (
  input  I1,
  input  I2,
  input  S,
  output x,
  output y
);

  wire and_1_out, and_2_out, and_3_out, and_4_out, not_1_out, not_2_out;

  not not_1 (not_1_out, S);
  not not_2 (not_2_out, S);
  and and_1 (and_1_out, I2, S);
  or or_1 (x, and_1_out, and_2_out);
  and and_2 (and_2_out, I1, not_1_out);
  and and_3 (and_3_out, I2, not_2_out);
  or or_2 (y, and_3_out, and_4_out);
  and and_4 (and_4_out, I1, S);
endmodule

module _4bit_swap (
  input  [3:0] in_1,
  input  [3:0] in_2,
  input  in_3,
  output [3:0] out_4,
  output [3:0] out_5
);

  _1bit_swap u_1bit_swap_1 (.I1(in_1[0]), .I2(in_2[0]), .S(in_3), .x(out_4[0]), .y(out_5[0]));
  _1bit_swap u_1bit_swap_2 (.I1(in_1[1]), .I2(in_2[1]), .S(in_3), .x(out_4[1]), .y(out_5[1]));
  _1bit_swap u_1bit_swap_3 (.I1(in_1[2]), .I2(in_2[2]), .S(in_3), .x(out_4[2]), .y(out_5[2]));
  _1bit_swap u_1bit_swap_4 (.I1(in_1[3]), .I2(in_2[3]), .S(in_3), .x(out_4[3]), .y(out_5[3]));

  // Other names for the same wires on the sheet: in1_0 = in_1[0]; in1_1 = in_1[1]; in1_2 = in_1[2]; in1_3 = in_1[3];
  //   in2_0 = in_2[0]; in2_1 = in_2[1]; in2_2 = in_2[2]; in2_3 = in_2[3]; out1_0 = out_4[0]; out1_1 = out_4[1];
  //   out1_2 = out_4[2]; out1_3 = out_4[3]; out2_0 = out_5[0]; out2_1 = out_5[1]; out2_2 = out_5[2];
  //   out2_3 = out_5[3]; switch = in_3
endmodule

module _4bit_sort (
  input  [3:0] in_1,
  input  [3:0] in_2,
  input  [3:0] in_3,
  input  [3:0] in_4,
  output [3:0] out_5,
  output [3:0] out_6,
  output [3:0] out_7,
  output [3:0] out_8
);

  wire compare_1_out_3, compare_2_out_3, compare_3_out_3, compare_4_out_3, compare_5_out_3, compare_6_out_3;
  wire [3:0] n4bit_swap_1_out_4, n4bit_swap_1_out_5, n4bit_swap_2_out_4, n4bit_swap_2_out_5,
       n4bit_swap_3_out_4, n4bit_swap_3_out_5, n4bit_swap_4_out_5, n4bit_swap_5_out_5;

  compare compare_1 (.in_1(in_1), .in_2(in_2), .out_3(compare_1_out_3));
  _4bit_swap u_4bit_swap_1 (
    .in_1(in_1), .in_2(in_2), .in_3(compare_1_out_3), .out_4(n4bit_swap_1_out_4), .out_5(n4bit_swap_1_out_5));
  compare compare_2 (.in_1(n4bit_swap_1_out_4), .in_2(in_3), .out_3(compare_2_out_3));
  _4bit_swap u_4bit_swap_2 (
    .in_1(n4bit_swap_1_out_4), .in_2(in_3), .in_3(compare_2_out_3), .out_4(n4bit_swap_2_out_4),
    .out_5(n4bit_swap_2_out_5));
  compare compare_3 (.in_1(n4bit_swap_2_out_5), .in_2(n4bit_swap_1_out_5), .out_3(compare_3_out_3));
  _4bit_swap u_4bit_swap_3 (
    .in_1(n4bit_swap_2_out_5), .in_2(n4bit_swap_1_out_5), .in_3(compare_3_out_3), .out_4(n4bit_swap_3_out_4),
    .out_5(n4bit_swap_3_out_5));
  _4bit_swap u_4bit_swap_4 (
    .in_1(n4bit_swap_2_out_4), .in_2(in_4), .in_3(compare_4_out_3), .out_4(out_5), .out_5(n4bit_swap_4_out_5));
  compare compare_4 (.in_1(n4bit_swap_2_out_4), .in_2(in_4), .out_3(compare_4_out_3));
  _4bit_swap u_4bit_swap_5 (
    .in_1(n4bit_swap_4_out_5), .in_2(n4bit_swap_3_out_4), .in_3(compare_5_out_3), .out_4(out_6),
    .out_5(n4bit_swap_5_out_5));
  compare compare_5 (.in_1(n4bit_swap_4_out_5), .in_2(n4bit_swap_3_out_4), .out_3(compare_5_out_3));
  compare compare_6 (.in_1(n4bit_swap_5_out_5), .in_2(n4bit_swap_3_out_5), .out_3(compare_6_out_3));
  _4bit_swap u_4bit_swap_6 (
    .in_1(n4bit_swap_5_out_5), .in_2(n4bit_swap_3_out_5), .in_3(compare_6_out_3), .out_4(out_7), .out_5(out_8));
endmodule

module compare (
  input  [3:0] in_1,
  input  [3:0] in_2,
  output out_3
);

  Comparator #(.width(4), .mode("unsigned")) comparator_1 (.a(in_1), .b(in_2), .lt(out_3));  // open: gt, eq
endmodule
