// Logisim project P0(former)_gcb.circ as structural Verilog: 2 circuits, main circuit main
module main (
  input  [7:0] in_1,
  input  [7:0] in_2,
  output [7:0] out_3,
  output [7:0] out_4
);

  Divider divider_1 (.a(in_1), .b(in_2), .rem(out_4));  // open: out, upper

  assign out_3 = in_2;
endmodule

module gcd (
  input  [7:0] in_1,
  input  [7:0] in_2,
  output [7:0] out_3
);

  wire clock_1_out, clock_2_out, clock_3_out, comparator_1_eq, comparator_2_eq, comparator_3_eq, count, flag,
       not_1_out, not_2_out, or_1_out;
  wire [7:0] main_1_out_3, main_1_out_4, multiplexer_1_out, multiplexer_2_out, multiplexer_3_out,
       register_1_q, register_2_q;

  Clock clock_1 (.out(clock_1_out));
  Multiplexer #(.width(8)) multiplexer_1 (
    .in0(in_1), .in1(register_1_q), .out(multiplexer_1_out), .sel(count));  // open: en
  Multiplexer #(.width(8)) multiplexer_2 (
    .in0(in_2), .in1(register_2_q), .out(multiplexer_2_out), .sel(count));  // open: en
  Counter #(.width(1), .max('h1), .ongoal("stay")) counter_1 (
    .Q(count), .clk(clock_1_out));  // open: load, D, count, carry, clr
  main main_1 (.in_1(multiplexer_1_out), .in_2(multiplexer_2_out), .out_3(main_1_out_3), .out_4(main_1_out_4));
  // Probe on main_1_out_3
  // Probe on main_1_out_4
  Clock clock_2 (.out(clock_2_out));
  Clock clock_3 (.out(clock_3_out));
  Register register_1 (.D(main_1_out_3), .en(flag), .Q(register_1_q), .clk(clock_2_out));  // open: clr
  Register register_2 (.D(main_1_out_4), .en(flag), .Q(register_2_q), .clk(clock_3_out));  // open: clr
  Comparator comparator_1 (.a(register_1_q), .b(8'h1), .eq(comparator_1_eq));  // open: gt, lt
  Comparator comparator_2 (.a(register_2_q), .b(8'h1), .eq(comparator_2_eq));  // open: gt, lt
  Comparator comparator_3 (.a(register_2_q), .b({8{1'b0}}), .eq(comparator_3_eq));  // open: gt, lt
  or or_1 (or_1_out, comparator_1_eq, comparator_2_eq);
  Multiplexer #(.width(8)) multiplexer_3 (
    .in0({8{1'b0}}), .in1(register_1_q), .out(multiplexer_3_out), .sel(comparator_3_eq));  // open: en
  not not_1 (not_1_out, comparator_3_eq);
  not not_2 (not_2_out, count);
  Multiplexer #(.width(8)) multiplexer_4 (
    .in0(multiplexer_3_out), .in1(8'h1), .out(out_3), .sel(or_1_out));  // open: en
  or or_2 (flag, not_1_out, not_2_out);
endmodule
