// Logisim project P0_3.circ as structural Verilog: 3 circuits, main circuit main
module main (
  input  [4:0] in_1,
  output [31:0] out_2
);

  wire clock_1_out, comparator_1_gt, not_1_out;
  wire [4:0] adder_1_out, counter_1_q;
  wire [31:0] store_1_out_4, store_1_out_5, trans_1_out_4;

  Clock clock_1 (.out(clock_1_out));
  Counter #(.width(5), .max('h1f), .ongoal("stay")) counter_1 (
    .Q(counter_1_q), .clk(clock_1_out));  // open: load, D, count, carry, clr
  trans trans_1 (.in_1(store_1_out_4), .in_2(store_1_out_5), .in_3(out_2), .out_4(trans_1_out_4));
  Adder #(.width(5)) adder_1 (.a(in_1), .b(5'b00001), .out(adder_1_out));  // open: cin, cout
  store store_1 (
    .in_1(trans_1_out_4), .in_2(clock_1_out), .in_3(not_1_out), .out_4(store_1_out_4), .out_5(store_1_out_5),
    .out_6(out_2));
  Comparator #(.width(5), .mode("unsigned")) comparator_1 (
    .a(counter_1_q), .b(adder_1_out), .gt(comparator_1_gt));  // open: eq, lt
  not not_1 (not_1_out, comparator_1_gt);
endmodule

module trans (
  input  [31:0] in_1,
  input  [31:0] in_2,
  input  [31:0] in_3,
  output [31:0] out_4
);

  wire [31:0] and_1_out;

  assign and_1_out = in_2 & in_3;  // AND_Gate and_1, 32 bits wide
  Adder #(.width(32)) adder_1 (.a(in_1), .b(and_1_out), .out(out_4));  // open: cin, cout
endmodule

module store (
  input  [31:0] in_1,
  input  in_2,
  input  in_3,
  output [31:0] out_4,
  output [31:0] out_5,
  output [31:0] out_6
);

  wire comparator_1_gt;
  wire [4:0] counter_1_q;
  wire [31:0] register_1_q, register_2_q, register_3_q;

  Register #(.width(32)) register_1 (.D(in_1), .en(in_3), .Q(register_1_q), .clk(in_2));  // open: clr
  Counter #(.width(5), .max('h1f), .ongoal("stay")) counter_1 (
    .Q(counter_1_q), .clk(in_2));  // open: load, D, count, carry, clr
  Register #(.width(32)) register_2 (.D(register_1_q), .en(in_3), .Q(register_2_q), .clk(in_2));  // open: clr
  Comparator #(.width(5), .mode("unsigned")) comparator_1 (
    .a(counter_1_q), .b({5{1'b0}}), .gt(comparator_1_gt));  // open: eq, lt
  Register #(.width(32)) register_3 (.D(register_2_q), .en(in_3), .Q(register_3_q), .clk(in_2));  // open: clr
  Multiplexer #(.width(32)) multiplexer_1 (
    .in0(32'h1), .in1(register_1_q), .out(out_4), .sel(comparator_1_gt));  // open: en
  Multiplexer #(.width(32)) multiplexer_2 (
    .in0(32'h1), .in1(register_2_q), .out(out_5), .sel(comparator_1_gt));  // open: en
  Multiplexer #(.width(32)) multiplexer_3 (
    .in0({32{1'b0}}), .in1(register_3_q), .out(out_6), .sel(comparator_1_gt));  // open: en
endmodule
