// Logisim project P0_ftoi.circ as structural Verilog: 1 circuit, main circuit ftoi
module ftoi (
  input  [15:0] in_1,
  output [31:0] out_2
);

  wire comparator_1_eq, comparator_2_eq, or_1_out, subtractor_1_bout;
  wire [4:0] subtractor_1_out;
  wire [10:0] bit_extender_2_out;
  wire [31:0] bit_extender_1_out, multiplexer_1_out, shifter_1_out, shifter_2_out, subtractor_2_out;

  Subtractor #(.width(5)) subtractor_1 (
    .a(in_1[14:10]), .b(5'b01111), .out(subtractor_1_out), .bout(subtractor_1_bout));  // open: bin
  // Probe on subtractor_1_out
  // Probe on bit_extender_1_out
  assign bit_extender_1_out = {{21{1'b0}}, bit_extender_2_out};  // Bit_Extender bit_extender_1
  assign bit_extender_2_out = {{1{1'b1}}, in_1[9:0]};  // Bit_Extender bit_extender_2
  Comparator #(.width(5)) comparator_1 (.a(in_1[14:10]), .b({5{1'b0}}), .eq(comparator_1_eq));  // open: gt, lt
  Comparator #(.width(5)) comparator_2 (.a(in_1[14:10]), .b({5{1'b1}}), .eq(comparator_2_eq));  // open: gt, lt
  Shifter #(.width(32)) shifter_1 (.in(bit_extender_1_out), .\dist (subtractor_1_out), .out(shifter_1_out));
  Shifter #(.width(32), .shift("lr")) shifter_2 (.in(shifter_1_out), .\dist (5'b01010), .out(shifter_2_out));
  or or_1 (or_1_out, comparator_1_eq, subtractor_1_bout, comparator_2_eq);
  Multiplexer #(.width(32)) multiplexer_1 (
    .in0(shifter_2_out), .in1({32{1'b0}}), .out(multiplexer_1_out), .sel(or_1_out));  // open: en
  // Probe on multiplexer_1_out
  Subtractor #(.width(32)) subtractor_2 (
    .a({32{1'b0}}), .b(multiplexer_1_out), .out(subtractor_2_out));  // open: bin, bout
  Multiplexer #(.width(32)) multiplexer_2 (
    .in0(multiplexer_1_out), .in1(subtractor_2_out), .out(out_2), .sel(in_1[15]));  // open: en

  // Other names for the same wires on the sheet: s = in_1[15]
endmodule
