// Logisim project 投票器.circ as structural Verilog: 1 circuit, main circuit main
module main (
  input  [1:0] A,
  input  [1:0] B,
  input  [1:0] C,
  input  [1:0] D,
  output out_5
);

  wire comparator_1_eq, comparator_2_eq, comparator_3_eq, comparator_4_eq, comparator_5_eq, comparator_6_eq,
       comparator_7_eq, comparator_8_eq, comparator_9_eq, comparator_10_eq, comparator_11_eq,
       comparator_12_lt, comparator_13_gt, or_1_out, or_2_out, or_3_out;
  wire [2:0] adder_1_out, adder_2_out, adder_3_out, adder_4_out, adder_5_out, adder_6_out,
       bit_extender_1_out, bit_extender_2_out, bit_extender_3_out, bit_extender_4_out, bit_extender_5_out,
       bit_extender_6_out, bit_extender_7_out, bit_extender_8_out;

  Comparator #(.width(2), .mode("unsigned")) comparator_1 (.a(A), .b(2'b00), .eq(comparator_1_eq));  // open: gt, lt
  Comparator #(.width(2), .mode("unsigned")) comparator_2 (.a(B), .b(2'b00), .eq(comparator_2_eq));  // open: gt, lt
  Comparator #(.width(2), .mode("unsigned")) comparator_3 (.a(C), .b(2'b00), .eq(comparator_3_eq));  // open: gt, lt
  Comparator #(.width(2), .mode("unsigned")) comparator_4 (.a(D), .b(2'b00), .eq(comparator_4_eq));  // open: gt, lt
  Comparator #(.width(2), .mode("unsigned")) comparator_5 (.a(A), .b(2'b01), .eq(comparator_5_eq));  // open: gt, lt
  Comparator #(.width(2), .mode("unsigned")) comparator_6 (.a(B), .b(2'b01), .eq(comparator_6_eq));  // open: gt, lt
  Comparator #(.width(2), .mode("unsigned")) comparator_7 (.a(B), .b(2'b11), .eq(comparator_7_eq));  // open: gt, lt
  Comparator #(.width(2), .mode("unsigned")) comparator_8 (.a(C), .b(2'b01), .eq(comparator_8_eq));  // open: gt, lt
  Comparator #(.width(2), .mode("unsigned")) comparator_9 (.a(C), .b(2'b11), .eq(comparator_9_eq));  // open: gt, lt
  Comparator #(.width(2), .mode("unsigned")) comparator_10 (.a(D), .b(2'b01), .eq(comparator_10_eq));  // open: gt, lt
  Comparator #(.width(2), .mode("unsigned")) comparator_11 (.a(D), .b(2'b11), .eq(comparator_11_eq));  // open: gt, lt
  assign bit_extender_1_out = {{2{1'b0}}, comparator_1_eq};  // Bit_Extender bit_extender_1
  Adder #(.width(3)) adder_1 (.a(bit_extender_1_out), .b(bit_extender_2_out), .out(adder_1_out));  // open: cin, cout
  assign bit_extender_2_out = {{2{1'b0}}, comparator_2_eq};  // Bit_Extender bit_extender_2
  assign bit_extender_3_out = {{2{1'b0}}, comparator_3_eq};  // Bit_Extender bit_extender_3
  assign bit_extender_4_out = {{2{1'b0}}, comparator_4_eq};  // Bit_Extender bit_extender_4
  assign bit_extender_5_out = {{2{1'b0}}, comparator_5_eq};  // Bit_Extender bit_extender_5
  assign bit_extender_6_out = {{2{1'b0}}, or_1_out};  // Bit_Extender bit_extender_6
  or or_1 (or_1_out, comparator_6_eq, comparator_7_eq);
  assign bit_extender_7_out = {{2{1'b0}}, or_2_out};  // Bit_Extender bit_extender_7
  or or_2 (or_2_out, comparator_8_eq, comparator_9_eq);
  assign bit_extender_8_out = {{2{1'b0}}, or_3_out};  // Bit_Extender bit_extender_8
  or or_3 (or_3_out, comparator_10_eq, comparator_11_eq);
  Adder #(.width(3)) adder_2 (.a(bit_extender_3_out), .b(bit_extender_4_out), .out(adder_2_out));  // open: cin, cout
  Adder #(.width(3)) adder_3 (.a(bit_extender_5_out), .b(bit_extender_6_out), .out(adder_3_out));  // open: cin, cout
  Adder #(.width(3)) adder_4 (.a(bit_extender_7_out), .b(bit_extender_8_out), .out(adder_4_out));  // open: cin, cout
  Adder #(.width(3)) adder_5 (.a(adder_1_out), .b(adder_2_out), .out(adder_5_out));  // open: cin, cout
  Adder #(.width(3)) adder_6 (.a(adder_3_out), .b(adder_4_out), .out(adder_6_out));  // open: cin, cout
  Comparator #(.width(2), .mode("unsigned")) comparator_12 (.a(A), .b(2'b11), .lt(comparator_12_lt));  // open: gt, eq
  Comparator #(.width(3), .mode("unsigned")) comparator_13 (
    .a(adder_5_out), .b(adder_6_out), .gt(comparator_13_gt));  // open: eq, lt
  and and_1 (out_5, comparator_12_lt, comparator_13_gt);
endmodule
