// Logisim project CPU0.circ as structural Verilog: 9 circuits, main circuit main
module main (
  input  in_1,
  output [31:0] out_2,
  output out_3,
  output [4:0] out_4,
  output [31:0] out_5,
  output out_6,
  output [4:0] out_7,
  output [31:0] out_8
);

  wire ALUSrc, Branch, Equal, EXTSelect, Greater, Jump, Less, MemToReg, PCSrc, RegDst;
  wire [2:0] ALUControl;
  wire [31:0] adder_1_out, alu_1_y, bit_extender_1_out, data_memory_1_rd, multiplexer_2_out,
       multiplexer_3_out, multiplexer_4_out, PC_prime, program_conter_1_pc, register_file_1_rd1, shiftResult;

  Adder #(.width(32)) adder_1 (.a(PC_prime), .b(shiftResult), .out(adder_1_out));  // open: cin, cout
  Control_Unit control_unit_1 (
    .opcode(out_2[31:26]), .funct(out_2[5:0]), .RegWrite(out_3), .RegDst(RegDst), .ALUSrc(ALUSrc),
    .Branch(Branch), .MemWrite(out_6), .MemtoReg(MemToReg), .EXTSelect(EXTSelect),
    .ALUControl2(ALUControl[2]), .ALUControl1(ALUControl[1]), .ALUControl0(ALUControl[0]), .Jump(Jump));
  Multiplexer #(.width(5)) multiplexer_1 (
    .in0(out_2[20:16]), .in1(out_2[15:11]), .out(out_4), .sel(RegDst));  // open: en
  Multiplexer #(.width(32)) multiplexer_2 (
    .in0(PC_prime), .in1(adder_1_out), .out(multiplexer_2_out), .sel(PCSrc));  // open: en
  Program_Conter program_conter_1 (.PC_prime(multiplexer_3_out), .PC(program_conter_1_pc), .reset(in_1));
  Multiplexer #(.width(32)) multiplexer_3 (
    .in0(multiplexer_2_out), .in1({{6{1'b0}}, out_2[25:0]}), .out(multiplexer_3_out), .sel(Jump));  // open: en
  Register_File register_file_1 (
    .in_3(out_2[25:21]), .in_4(out_2[20:16]), .in_5(out_4), .in_6(out_5), .RD2(out_8),
    .RD1(register_file_1_rd1), .in_1(out_3), .in_2(in_1));
  Bit_Extender bit_extender_1 (.in(out_2[15:0]), .out(bit_extender_1_out), .EXTSelect(EXTSelect));
  Instruction_Memory instruction_memory_1 (.A(program_conter_1_pc), .D(out_2));
  Adder #(.width(32)) adder_2 (.a(program_conter_1_pc), .b(32'h4), .out(PC_prime));  // open: cin, cout
  and and_1 (PCSrc, Branch, Equal);
  Multiplexer #(.width(32)) multiplexer_4 (
    .in0(out_8), .in1(bit_extender_1_out), .out(multiplexer_4_out), .sel(ALUSrc));  // open: en
  Shifter #(.width(32)) shifter_1 (.in(bit_extender_1_out), .\dist (5'b00010), .out(shiftResult));
  ALU alu_1 (
    .A(register_file_1_rd1), .B(multiplexer_4_out), .op(ALUControl),
    .Y({alu_1_y[31:7], out_7, alu_1_y[1:0]}), .Zero(Equal), .less(Greater), .greater(Less));
  Data_Memory data_memory_1 (
    .reset(in_1), .WE(out_6), .A({alu_1_y[31:7], out_7, alu_1_y[1:0]}), .WD(out_8), .RD(data_memory_1_rd));
  Multiplexer #(.width(32)) multiplexer_5 (
    .in0({alu_1_y[31:7], out_7, alu_1_y[1:0]}), .in1(data_memory_1_rd), .out(out_5), .sel(MemToReg));  // open: en

  // Other names for the same wires on the sheet: MemAddr[4:0] = out_7; Instr[31:0] = out_2;
  //   opcode[5:0] = out_2[31:26]; funct[5:0] = out_2[5:0]; jumpAdd[25:0] = out_2[25:0]; offset[15:0] = out_2[15:0];
  //   shamt[4:0] = out_2[10:6]; rd[4:0] = out_2[15:11]; rt[4:0] = out_2[20:16]; rs[4:0] = out_2[25:21];
  //   MemData[31:0] = out_8; MemWrite = out_6; RegAddr[4:0] = out_4; RegData[31:0] = out_5; RegWrite = out_3;
  //   Reset = in_1

  // Notes on the sheet:
  //   指令数*4=地址偏移量
endmodule

// PC
module Program_Conter (
  input  [31:0] PC_prime,
  input  reset,
  output [31:0] PC
);

  wire clock_1_out;

  Register #(.width(32)) register_1 (.D(PC_prime), .Q(PC), .clk(clock_1_out), .clr(reset));  // open: en
  Clock clock_1 (.out(clock_1_out));
endmodule

// IM
module Instruction_Memory (
  input  [31:0] A,
  output [31:0] D
);

  ROM #(.addrWidth(5), .dataWidth(32)) rom_1 (.addr(A[6:2]), .data(D));  // open: sel

  // Notes on the sheet:
  //   contents of rom_1 (hex, n*v repeats v):
  //   341c0000 341d0000 ac010000 ac080000 34013456 210820 8c010004 ac010004 3c027878 411822 3c051234
  //   34040005 0 ac85ffff 8c83ffff 10650001 1000000d 34670404 10e3000b 0 3c087777 3508ffff 80022 34001100
  //   e65020 34080000 34090001 340a0001 10a4020 1109fffe 1000ffff
endmodule

// GRF
module Register_File (
  input  in_1,
  input  in_2,
  input  [4:0] in_3,
  input  [4:0] in_4,
  input  [4:0] in_5,
  input  [31:0] in_6,
  output [31:0] RD2,
  output [31:0] RD1
);

  wire clk;
  wire [31:0] r0_out, r1, r1_out, r2, r2_out, r3, r3_out, r4, r4_out, r5, r5_out, r6, r6_out, r7, r7_out, r8,
       r8_out, r9, r9_out, r10, r10_out, r11, r11_out, r12, r12_out, r13, r13_out, r14, r14_out, r15,
       r15_out, r16, r16_out, r17, r17_out, r18, r18_out, r19, r19_out, r20, r20_out, r21, r21_out, r22,
       r22_out, r23, r23_out, r24, r24_out, r25, r25_out, r26, r26_out, r27, r27_out, r28, r28_out, r29,
       r29_out, r30, r30_out, r31, r31_out;

  Clock clock_1 (.out(clk));
  Demultiplexer #(.select(5), .width(32), .tristate("true")) demultiplexer_1 (
    .out1(r1), .out2(r2), .out3(r3), .out4(r4), .out5(r5), .out6(r6), .out7(r7), .out8(r8), .out9(r9),
    .out10(r10), .out11(r11), .out12(r12), .out13(r13), .out14(r14), .out15(r15), .out16(r16), .out17(r17),
    .out18(r18), .out19(r19), .out20(r20), .out21(r21), .out22(r22), .out23(r23), .out24(r24), .out25(r25),
    .out26(r26), .out27(r27), .out28(r28), .out29(r29), .out30(r30), .out31(r31), .in(in_6), .sel(in_5),
    .en(in_1));  // open: out0
  Register #(.width(32)) register_1 (.D({32{1'b0}}), .Q(r0_out), .clk(clk), .clr(in_2));  // open: en
  Register #(.width(32)) register_2 (.D(r1), .Q(r1_out), .clk(clk), .clr(in_2));  // open: en
  Register #(.width(32)) register_3 (.D(r2), .Q(r2_out), .clk(clk), .clr(in_2));  // open: en
  Register #(.width(32)) register_4 (.D(r3), .Q(r3_out), .clk(clk), .clr(in_2));  // open: en
  Register #(.width(32)) register_5 (.D(r4), .Q(r4_out), .clk(clk), .clr(in_2));  // open: en
  Register #(.width(32)) register_6 (.D(r5), .Q(r5_out), .clk(clk), .clr(in_2));  // open: en
  Register #(.width(32)) register_7 (.D(r6), .Q(r6_out), .clk(clk), .clr(in_2));  // open: en
  Register #(.width(32)) register_8 (.D(r7), .Q(r7_out), .clk(clk), .clr(in_2));  // open: en
  Register #(.width(32)) register_9 (.D(r8), .Q(r8_out), .clk(clk), .clr(in_2));  // open: en
  Register #(.width(32)) register_10 (.D(r9), .Q(r9_out), .clk(clk), .clr(in_2));  // open: en
  Register #(.width(32)) register_11 (.D(r10), .Q(r10_out), .clk(clk), .clr(in_2));  // open: en
  Register #(.width(32)) register_12 (.D(r11), .Q(r11_out), .clk(clk), .clr(in_2));  // open: en
  Register #(.width(32)) register_13 (.D(r12), .Q(r12_out), .clk(clk), .clr(in_2));  // open: en
  Register #(.width(32)) register_14 (.D(r13), .Q(r13_out), .clk(clk), .clr(in_2));  // open: en
  Register #(.width(32)) register_15 (.D(r14), .Q(r14_out), .clk(clk), .clr(in_2));  // open: en
  Register #(.width(32)) register_16 (.D(r15), .Q(r15_out), .clk(clk), .clr(in_2));  // open: en
  Multiplexer #(.select(5), .width(32), .disabled(0)) multiplexer_1 (
    .in0(r0_out), .in1(r1_out), .in2(r2_out), .in3(r3_out), .in4(r4_out), .in5(r5_out), .in6(r6_out),
    .in7(r7_out), .in8(r8_out), .in9(r9_out), .in10(r10_out), .in11(r11_out), .in12(r12_out), .in13(r13_out),
    .in14(r14_out), .in15(r15_out), .in16(r16_out), .in17(r17_out), .in18(r18_out), .in19(r19_out),
    .in20(r20_out), .in21(r21_out), .in22(r22_out), .in23(r23_out), .in24(r24_out), .in25(r25_out),
    .in26(r26_out), .in27(r27_out), .in28(r28_out), .in29(r29_out), .in30(r30_out), .in31(r31_out),
    .out(RD1), .sel(in_3), .en(1'b1));
  Register #(.width(32)) register_17 (.D(r16), .Q(r16_out), .clk(clk), .clr(in_2));  // open: en
  Register #(.width(32)) register_18 (.D(r17), .Q(r17_out), .clk(clk), .clr(in_2));  // open: en
  Register #(.width(32)) register_19 (.D(r18), .Q(r18_out), .clk(clk), .clr(in_2));  // open: en
  Register #(.width(32)) register_20 (.D(r19), .Q(r19_out), .clk(clk), .clr(in_2));  // open: en
  Register #(.width(32)) register_21 (.D(r20), .Q(r20_out), .clk(clk), .clr(in_2));  // open: en
  Register #(.width(32)) register_22 (.D(r21), .Q(r21_out), .clk(clk), .clr(in_2));  // open: en
  Register #(.width(32)) register_23 (.D(r22), .Q(r22_out), .clk(clk), .clr(in_2));  // open: en
  Register #(.width(32)) register_24 (.D(r23), .Q(r23_out), .clk(clk), .clr(in_2));  // open: en
  Register #(.width(32)) register_25 (.D(r24), .Q(r24_out), .clk(clk), .clr(in_2));  // open: en
  Register #(.width(32)) register_26 (.D(r25), .Q(r25_out), .clk(clk), .clr(in_2));  // open: en
  Register #(.width(32)) register_27 (.D(r26), .Q(r26_out), .clk(clk), .clr(in_2));  // open: en
  Register #(.width(32)) register_28 (.D(r27), .Q(r27_out), .clk(clk), .clr(in_2));  // open: en
  Multiplexer #(.select(5), .width(32), .disabled(0)) multiplexer_2 (
    .in0(r0_out), .in1(r1_out), .in2(r2_out), .in3(r3_out), .in4(r4_out), .in5(r5_out), .in6(r6_out),
    .in7(r7_out), .in8(r8_out), .in9(r9_out), .in10(r10_out), .in11(r11_out), .in12(r12_out), .in13(r13_out),
    .in14(r14_out), .in15(r15_out), .in16(r16_out), .in17(r17_out), .in18(r18_out), .in19(r19_out),
    .in20(r20_out), .in21(r21_out), .in22(r22_out), .in23(r23_out), .in24(r24_out), .in25(r25_out),
    .in26(r26_out), .in27(r27_out), .in28(r28_out), .in29(r29_out), .in30(r30_out), .in31(r31_out),
    .out(RD2), .sel(in_4), .en(1'b1));
  Register #(.width(32)) register_29 (.D(r28), .Q(r28_out), .clk(clk), .clr(in_2));  // open: en
  Register #(.width(32)) register_30 (.D(r29), .Q(r29_out), .clk(clk), .clr(in_2));  // open: en
  Register #(.width(32)) register_31 (.D(r30), .Q(r30_out), .clk(clk), .clr(in_2));  // open: en
  Register #(.width(32)) register_32 (.D(r31), .Q(r31_out), .clk(clk), .clr(in_2));  // open: en

  // Other names for the same wires on the sheet: A1[4:0] = in_3; A2[4:0] = in_4; A3[4:0] = in_5; clr = in_2;
  //   WD[31:0] = in_6; WE = in_1
endmodule

// DM
module Data_Memory (
  input  [31:0] A,
  input  [31:0] WD,
  input  WE,
  input  reset,
  output [31:0] RD
);

  wire clock_1_out, not_1_out;

  Clock clock_1 (.out(clock_1_out));
  not not_1 (not_1_out, WE);
  RAM #(.addrWidth(5), .dataWidth(32), .bus("separate")) ram_1 (
    .addr(A[6:2]), .din(WD), .data(RD), .str(WE), .clk(clock_1_out), .ld(not_1_out), .clr(reset));  // open: sel
endmodule

module ALU (
  input  [2:0] op,
  input  [31:0] A,
  input  [31:0] B,
  output greater,
  output Zero,
  output less,
  output [31:0] Y
);

  wire [31:0] adder_1_out, or_1_out, shifter_1_out, subtractor_1_out;

  Comparator #(.width(32), .mode("unsigned")) comparator_1 (.a(A), .b(B), .gt(greater), .eq(Zero), .lt(less));
  Adder #(.width(32)) adder_1 (.a(A), .b(B), .out(adder_1_out));  // open: cin, cout
  Subtractor #(.width(32)) subtractor_1 (.a(A), .b(B), .out(subtractor_1_out));  // open: bin, bout
  assign or_1_out = A | B;  // OR_Gate or_1, 32 bits wide
  Shifter #(.width(32)) shifter_1 (.in(B), .\dist (5'b10000), .out(shifter_1_out));
  Multiplexer #(.select(3), .width(32)) multiplexer_1 (
    .in0(adder_1_out), .in1(subtractor_1_out), .in2(or_1_out), .in3(shifter_1_out), .out(Y), .sel(op));  // open: in4, in5, in6, in7, en
endmodule

// EXT
module Bit_Extender (
  input  EXTSelect,
  input  [15:0] in,
  output [31:0] out
);

  wire [31:0] bit_extender_1_out, bit_extender_2_out;

  assign bit_extender_1_out = {{16{in[15]}}, in};  // Bit_Extender_part bit_extender_1
  assign bit_extender_2_out = {{16{1'b0}}, in};  // Bit_Extender_part bit_extender_2
  Multiplexer #(.width(32)) multiplexer_1 (
    .in0(bit_extender_1_out), .in1(bit_extender_2_out), .out(out), .sel(EXTSelect));  // open: en
endmodule

// CU
module Control_Unit (
  input  [5:0] opcode,
  input  [5:0] funct,
  output RegWrite,
  output RegDst,
  output ALUSrc,
  output Branch,
  output MemWrite,
  output MemtoReg,
  output EXTSelect,
  output Jump,
  output ALUControl2,
  output ALUControl1,
  output ALUControl0
);

  wire add_out, beq_out, comparator_1_eq, j_out, lui_out, lw_out, not_1_out, not_2_out, not_3_out, not_4_out,
       not_5_out, not_6_out, not_7_out, not_8_out, not_9_out, not_10_out, not_11_out, not_12_out, ori_out,
       sltu_out, sub_out, sw_out;

  not not_1 (not_1_out, opcode[5]);
  Comparator #(.width(6)) comparator_1 (.a({6{1'b0}}), .b(opcode), .eq(comparator_1_eq));  // open: gt, lt
  not not_2 (not_2_out, opcode[4]);
  not not_3 (not_3_out, opcode[2]);
  not not_4 (not_4_out, opcode[3]);
  not not_5 (not_5_out, opcode[1]);
  not not_6 (not_6_out, opcode[0]);
  not not_7 (not_7_out, funct[5]);
  not not_8 (not_8_out, funct[4]);
  not not_9 (not_9_out, funct[3]);
  not not_10 (not_10_out, funct[2]);
  not not_11 (not_11_out, funct[1]);
  not not_12 (not_12_out, funct[0]);
  and add (add_out, comparator_1_eq, funct[5], not_8_out, not_9_out, not_10_out, not_11_out, not_12_out);
  and sub (sub_out, comparator_1_eq, funct[5], not_8_out, not_9_out, not_10_out, funct[1], not_12_out);
  and ori (ori_out, not_1_out, not_2_out, opcode[3], opcode[2], not_5_out, opcode[0]);
  and lw (lw_out, opcode[5], not_2_out, not_4_out, not_3_out, opcode[1], opcode[0]);
  and sw (sw_out, opcode[5], not_2_out, opcode[3], not_3_out, opcode[1], opcode[0]);
  and beq (beq_out, not_1_out, not_2_out, not_4_out, opcode[2], not_5_out, not_6_out);
  and lui (lui_out, not_1_out, not_2_out, opcode[3], opcode[2], opcode[1], opcode[0]);
  and sltu (sltu_out, comparator_1_eq, funct[5], not_8_out, not_9_out, not_10_out, not_11_out, not_12_out);
  and j (j_out, not_1_out, not_2_out, not_4_out, not_3_out, opcode[1], not_6_out);
  or or_1 (RegWrite, 1'b0, add_out, sub_out, ori_out, lw_out, lui_out);
  or or_2 (RegDst, 1'b0, add_out, sub_out);
  or or_3 (ALUSrc, 1'b0, ori_out, lw_out, sw_out, lui_out);
  or or_4 (Branch, 1'b0, beq_out);
  or or_5 (MemWrite, 1'b0, sw_out);
  or or_6 (MemtoReg, 1'b0, lw_out);
  or or_7 (EXTSelect, 1'b0, ori_out, lui_out);
  or or_8 (Jump, 1'b0, j_out);
  buf or_9 (ALUControl2, 1'b0);  // OR_Gate
  or or_10 (ALUControl1, 1'b0, ori_out, lui_out);
  or or_11 (ALUControl0, 1'b0, sub_out, lui_out);
endmodule

// ACU
module ALU_Control_Unit (
  input  [1:0] ALUop,
  input  [5:0] funct
);

  wire not_1_out, not_2_out, not_3_out, not_4_out, not_5_out, not_6_out, not_7_out, not_8_out;

  not not_1 (not_1_out, ALUop[1]);
  not not_2 (not_2_out, ALUop[0]);
  not not_3 (not_3_out, funct[5]);
  not not_4 (not_4_out, funct[3]);
  not not_5 (not_5_out, funct[4]);
  not not_6 (not_6_out, funct[2]);
  not not_7 (not_7_out, funct[1]);
  not not_8 (not_8_out, funct[0]);
  // AND_Gate addu has open pins: in0=not_1_out, in1=not_2_out, in2=not_3_out, in3=not_5_out, in4=not_6_out, in5=not_7_out, in6=not_8_out, out=open
  // AND_Gate subu has open pins: in1=not_3_out, in2=not_5_out, in3=not_4_out, in4=not_6_out, in5=not_7_out, in6=not_8_out, out=open
  // AND_Gate ori has open pins: in1=not_3_out, in2=not_5_out, in3=funct[3], in4=funct[2], in5=not_7_out, in6=funct[0], out=open
  // AND_Gate lw has open pins: in1=funct[5], in2=not_5_out, in3=not_4_out, in4=not_6_out, in5=funct[1], in6=funct[0], out=open
  // AND_Gate sw has open pins: in1=funct[5], in2=not_5_out, in3=funct[3], in4=not_6_out, in5=funct[1], in6=funct[0], out=open
  // AND_Gate beq has open pins: in1=not_3_out, in2=not_5_out, in3=not_4_out, in4=funct[2], in5=not_7_out, in6=not_8_out, out=open
  // AND_Gate lui has open pins: in1=not_3_out, in2=not_5_out, in3=funct[3], in4=funct[2], in5=funct[1], in6=funct[0], out=open
endmodule
