// Logisim project 24-bit_selector.circ as structural Verilog: 1 circuit, main circuit main
module main (
  input  E,
  input  D,
  input  C,
  input  B,
  input  A,
  output F_A_B_C_D_E
);

  wire and_1_out, and_2_out, and_3_out, multiplexer_1_out, multiplexer_2_out, multiplexer_3_out, not_1_out,
       not_2_out;

  not not_1 (not_1_out, E);
  and and_1 (and_1_out, not_1_out, D);
  and and_2 (and_2_out, not_1_out, not_2_out);
  not not_2 (not_2_out, D);
  Multiplexer #(.select(3), .disabled(0)) multiplexer_1 (
    .in0(1'b0), .in1(1'b1), .in2(1'b0), .in3(1'b1), .in4(1'b0), .in5(1'b1), .in6(1'b0), .in7(1'b1),
    .out(multiplexer_1_out), .sel({C, B, A}), .en(and_2_out));
  Multiplexer #(.select(3), .disabled(0)) multiplexer_2 (
    .in0(1'b1), .in1(1'b0), .in2(1'b1), .in3(1'b0), .in4(1'b1), .in5(1'b0), .in6(1'b1), .in7(1'b0),
    .out(multiplexer_2_out), .sel({C, B, A}), .en(and_1_out));
  Multiplexer #(.select(3), .disabled(0)) multiplexer_3 (
    .in0(1'b1), .in1(1'b1), .in2(1'b1), .in3(1'b1), .in4(1'b1), .in5(1'b1), .in6(1'b1), .in7(1'b1),
    .out(multiplexer_3_out), .sel({C, B, A}), .en(and_3_out));
  and and_3 (and_3_out, E, D);
  or or_1 (F_A_B_C_D_E, multiplexer_1_out, multiplexer_2_out, multiplexer_3_out);
endmodule
