// Logisim project fib.circ as structural Verilog: 4 circuits, main circuit main2
module main2 (
  input  [2:0] in_1,
  output [3:0] out_2
);

  wire a, b, clock_1_out, counter_2_q;
  wire [2:0] subtractor_1_out;
  wire [3:0] adder_1_out, bit_extender_1_out, counter_1_q, multiplexer_1_out, ram_1_data, ram_2_data,
       subtractor_2_out;

  assign bit_extender_1_out = {{1{1'b0}}, subtractor_1_out};  // Bit_Extender bit_extender_1
  Subtractor #(.width(3)) subtractor_1 (.a(in_1), .b(3'b001), .out(subtractor_1_out));  // open: bin, bout
  not not_1 (b, a);
  Counter #(.width(4), .max('hf), .ongoal("stay")) counter_1 (
    .Q(counter_1_q), .clk(clock_1_out));  // open: load, D, count, carry, clr
  Comparator #(.width(4), .mode("unsigned")) comparator_1 (
    .a(bit_extender_1_out), .b(counter_1_q), .lt(a));  // open: gt, eq
  Clock clock_1 (.out(clock_1_out));
  Counter #(.width(1), .max('h1), .ongoal("stay")) counter_2 (
    .Q(counter_2_q), .clk(clock_1_out));  // open: load, D, count, carry, clr
  Multiplexer #(.width(4)) multiplexer_1 (
    .in0(4'b0001), .in1(adder_1_out), .out(multiplexer_1_out), .sel(counter_2_q));  // open: en
  RAM #(.addrWidth(2), .dataWidth(4), .bus("separate")) ram_1 (
    .addr(2'b00), .din(multiplexer_1_out), .data(ram_1_data), .str(b), .clk(clock_1_out));  // open: sel, ld, clr
  RAM #(.addrWidth(2), .dataWidth(4), .bus("separate")) ram_2 (
    .addr(2'b00), .din(subtractor_2_out), .data(ram_2_data), .str(b), .clk(clock_1_out));  // open: sel, ld, clr
  Adder #(.width(4)) adder_1 (.a(ram_1_data), .b(ram_2_data), .out(adder_1_out));  // open: cin, cout
  Multiplexer #(.width(4)) multiplexer_2 (.in0(4'b0000), .in1(ram_1_data), .out(out_2), .sel(a));  // open: en
  Subtractor #(.width(4)) subtractor_2 (.a(adder_1_out), .b(ram_2_data), .out(subtractor_2_out));  // open: bin, bout
endmodule

module \计算逻辑  (
  input  in_1,
  input  in_2,
  output [3:0] out_3
);

  wire enable, initialize;
  wire [3:0] adder_1_out, multiplexer_1_out, prev;

  Counter #(.width(1), .max('h1), .ongoal("stay")) counter_1 (
    .Q(initialize), .clk(in_2));  // open: load, D, count, carry, clr
  not not_1 (enable, in_1);
  Multiplexer #(.width(4)) multiplexer_1 (
    .in0(4'b0001), .in1(out_3), .out(multiplexer_1_out), .sel(initialize));  // open: en
  Register #(.width(4)) register_1 (.D(multiplexer_1_out), .en(enable), .Q(prev), .clk(in_2));  // open: clr
  Adder #(.width(4)) adder_1 (.a(out_3), .b(prev), .out(adder_1_out));  // open: cin, cout
  Register #(.width(4)) register_2 (.D(adder_1_out), .en(enable), .Q(out_3), .clk(in_2));  // open: clr

  // Other names for the same wires on the sheet: clk = in_2; now[3:0] = out_3
endmodule

module \计数逻辑  (
  input  [2:0] in_1,
  input  in_2,
  output out_3
);

  wire [3:0] bit_extender_1_out, counter_1_q;

  Counter #(.width(4), .max('hf), .ongoal("stay")) counter_1 (
    .Q(counter_1_q), .clk(in_2));  // open: load, D, count, carry, clr
  assign bit_extender_1_out = {{1{1'b0}}, in_1};  // Bit_Extender bit_extender_1
  Comparator #(.width(4), .mode("unsigned")) comparator_1 (
    .a(bit_extender_1_out), .b(counter_1_q), .lt(out_3));  // open: gt, eq
endmodule

module main (
  input  [2:0] in_1,
  output [3:0] out_2
);

  wire clock_1_out, \计数逻辑_1_out_3 ;
  wire [3:0] \计算逻辑_1_out_3 ;

  Clock clock_1 (.out(clock_1_out));
  \计数逻辑  \u_计数逻辑_1  (.in_1(in_1), .in_2(clock_1_out), .out_3(\计数逻辑_1_out_3 ));
  \计算逻辑  \u_计算逻辑_1  (.in_1(\计数逻辑_1_out_3 ), .in_2(clock_1_out), .out_3(\计算逻辑_1_out_3 ));
  Multiplexer #(.width(4)) multiplexer_1 (
    .in0(4'b0000), .in1(\计算逻辑_1_out_3 ), .out(out_2), .sel(\计数逻辑_1_out_3 ));  // open: en
endmodule
